// Logisim project BCD to 7-Segment Decoder Corrected.circ as structural Verilog: 2 circuits, main circuit main
module main (
  input  A,
  input  B,
  input  C,
  input  D,
  output a_2,
  output b_2,
  output c_2,
  output d_2,
  output e,
  output f,
  output g
);

  wire and_1_out, and_2_out, and_3_out, and_4_out, and_5_out, and_6_out, and_7_out, and_8_out, and_9_out,
       not_1_out, not_2_out, not_3_out, not_4_out;

  not not_1 (not_1_out, A);
  not not_2 (not_2_out, B);
  not not_3 (not_3_out, C);
  not not_4 (not_4_out, D);
  and and_1 (and_1_out, B, not_3_out);
  and and_2 (and_2_out, B, not_4_out);
  and and_3 (and_3_out, B, D);
  and and_4 (and_4_out, not_2_out, not_4_out);
  and and_5 (and_5_out, C, D);
  and and_6 (and_6_out, not_3_out, not_4_out);
  or or_1 (c_2, B, not_3_out, D);
  and and_7 (and_7_out, C, not_4_out);
  and and_8 (and_8_out, not_2_out, C);
  and and_9 (and_9_out, D, and_1_out);
  or or_2 (a_2, and_3_out, and_4_out, A, C);
  or or_3 (b_2, and_5_out, not_2_out, and_6_out);
  or or_4 (d_2, A, and_4_out, and_7_out, and_8_out, and_9_out);
  or or_5 (e, and_7_out, and_4_out);
  or or_6 (f, and_6_out, and_2_out, and_1_out, A);
  or or_7 (g, and_7_out, and_1_out, A, and_8_out);

  // Notes on the sheet:
  //   BCD to 7-Segment Decoder
endmodule

module _7_Segment_Display (
  input  in_1,
  input  in_2,
  input  in_3,
  input  in_4
);

  wire main_1_a_2, main_1_b_2, main_1_c_2, main_1_d_2, main_1_e, main_1_f, main_1_g;

  main main_1 (
    .A(in_1), .B(in_2), .C(in_3), .D(in_4), .a_2(main_1_a_2), .b_2(main_1_b_2), .c_2(main_1_c_2),
    .d_2(main_1_d_2), .e(main_1_e), .f(main_1_f), .g(main_1_g));
  _7_Segment_Display_part u_7_segment_display_1 (
    .g(main_1_g), .f(main_1_f), .a(main_1_a_2), .b(main_1_b_2), .e(main_1_e), .d(main_1_d_2), .c(main_1_c_2));  // open: dp
endmodule
