// Logisim project 3 x 8 Decoder.circ as structural Verilog: 1 circuit, main circuit main
module main (
  input  I_P_1,
  input  I_P_2,
  input  I_P_3,
  output O_P_1,
  output O_P_2,
  output O_P_3,
  output O_P_4,
  output O_P_5,
  output O_P_6,
  output O_P_7,
  output O_P_8
);

  wire not_1_out, not_2_out, not_3_out;

  not not_1 (not_1_out, I_P_1);
  not not_2 (not_2_out, I_P_2);
  not not_3 (not_3_out, I_P_3);
  and and_1 (O_P_1, not_1_out, not_2_out, not_3_out);
  and and_2 (O_P_2, not_1_out, not_2_out, I_P_3);
  and and_3 (O_P_3, not_1_out, I_P_2, not_3_out);
  and and_4 (O_P_4, not_1_out, I_P_2, I_P_3);
  and and_5 (O_P_5, I_P_1, not_2_out, not_3_out);
  and and_6 (O_P_6, I_P_1, not_2_out, I_P_3);
  and and_7 (O_P_7, I_P_1, I_P_2, not_3_out);
  and and_8 (O_P_8, I_P_1, I_P_2, I_P_3);

  // Notes on the sheet:
  //   3x8 Decoder
endmodule
