// Logisim project Gray to Binary Code Conversion.circ as structural Verilog: 1 circuit, main circuit main
module main (
  input  G4,
  input  G3,
  input  G2,
  input  G1
);

  wire xor_1_out, xor_2_out, xor_3_out;

  xor xor_1 (xor_1_out, G4, xor_2_out);
  xor xor_2 (xor_2_out, G3, xor_3_out);
  xor xor_3 (xor_3_out, G2, G1);
  LED led_1 (.in(xor_1_out));
  LED led_2 (.in(xor_2_out));
  LED led_3 (.in(xor_3_out));
  LED led_4 (.in(G1));

  // Notes on the sheet:
  //   Gray to Binary Code Conversion
  //   B4
  //   B3
  //   B2
  //   B1
endmodule
