// Logisim project Hexadecimal To 7-Segment Decoder.circ as structural Verilog: 2 circuits, main circuit Binary to Hexadecimal
module Binary_to_Hexadecimal (
  input  A,
  input  B,
  input  C,
  input  D,
  output a_2,
  output b_2,
  output c_2,
  output d_2,
  output e,
  output f,
  output g
);

  wire and_1_out, and_2_out, and_3_out, and_4_out, and_5_out, and_6_out, and_7_out, and_8_out, and_9_out,
       and_10_out, and_11_out, and_12_out, and_13_out, and_14_out, and_15_out, and_16_out, and_17_out,
       and_18_out, and_19_out, and_20_out, and_21_out, and_22_out, and_23_out, and_24_out, and_25_out,
       and_26_out, and_27_out, and_28_out, and_29_out, and_30_out, and_31_out, and_32_out, and_33_out,
       not_1_out, not_2_out, not_3_out, not_4_out, or_1_out, or_2_out, or_3_out, or_4_out, or_5_out,
       or_6_out, or_7_out, or_8_out, or_9_out, or_10_out, or_11_out, or_12_out, or_13_out, or_14_out,
       or_15_out, or_16_out, or_17_out;

  not not_1 (not_1_out, A);
  not not_2 (not_2_out, B);
  not not_3 (not_3_out, C);
  not not_4 (not_4_out, D);
  and and_1 (and_1_out, not_1_out, not_2_out);
  and and_2 (and_2_out, not_3_out, D);
  and and_3 (and_3_out, not_1_out, B);
  and and_4 (and_4_out, not_3_out, not_4_out);
  and and_5 (and_5_out, A, not_2_out);
  and and_6 (and_6_out, C, D);
  and and_7 (and_7_out, A, B);
  and and_8 (and_8_out, B, C);
  and and_9 (and_9_out, A, C);
  and and_10 (and_10_out, C, not_4_out);
  and and_11 (and_11_out, not_1_out, D);
  and and_12 (and_12_out, not_2_out, not_3_out);
  and and_13 (and_13_out, not_1_out, C);
  and and_14 (and_14_out, and_1_out, and_2_out);
  and and_15 (and_15_out, and_3_out, and_4_out);
  and and_16 (and_16_out, and_5_out, and_6_out);
  and and_17 (and_17_out, and_7_out, and_2_out);
  and and_18 (and_18_out, and_3_out, and_2_out);
  and and_19 (and_19_out, and_8_out, not_4_out);
  and and_20 (and_20_out, and_9_out, D);
  and and_21 (and_21_out, and_7_out, not_4_out);
  and and_22 (and_22_out, and_1_out, and_10_out);
  and and_23 (and_23_out, and_7_out, C);
  and and_24 (and_24_out, and_8_out, D);
  and and_25 (and_25_out, and_10_out, and_5_out);
  and and_26 (and_26_out, and_12_out, D);
  and and_27 (and_27_out, and_3_out, not_3_out);
  and and_28 (and_28_out, and_1_out, D);
  and and_29 (and_29_out, and_1_out, C);
  and and_30 (and_30_out, and_13_out, D);
  and and_31 (and_31_out, and_1_out, not_3_out);
  and and_32 (and_32_out, and_3_out, and_6_out);
  and and_33 (and_33_out, and_7_out, and_4_out);
  or or_1 (or_1_out, and_14_out, and_15_out);
  or or_2 (or_2_out, and_16_out, and_17_out);
  or or_3 (or_3_out, and_18_out, and_19_out);
  or or_4 (or_4_out, and_20_out, and_21_out);
  or or_5 (or_5_out, and_21_out, and_22_out);
  or or_6 (or_6_out, and_24_out, and_25_out);
  or or_7 (or_7_out, and_11_out, and_26_out);
  or or_8 (or_8_out, and_28_out, and_29_out);
  or or_9 (or_9_out, and_30_out, and_17_out);
  or or_10 (or_10_out, and_31_out, and_32_out);
  or or_11 (or_11_out, or_1_out, or_2_out);
  or or_12 (or_12_out, or_3_out, or_4_out);
  or or_13 (or_13_out, or_5_out, and_23_out);
  or or_14 (or_14_out, or_1_out, or_6_out);
  or or_15 (or_15_out, or_7_out, and_27_out);
  or or_16 (or_16_out, or_8_out, or_9_out);
  or or_17 (or_17_out, or_10_out, and_33_out);
  not not_5 (a_2, or_11_out);
  not not_6 (b_2, or_12_out);
  not not_7 (c_2, or_13_out);
  not not_8 (d_2, or_14_out);
  not not_9 (e, or_15_out);
  not not_10 (f, or_16_out);
  not not_11 (g, or_17_out);
endmodule

module Check_IC (
  input  in_1,
  input  in_2,
  input  in_3,
  input  in_4
);

  wire binary_to_hexadecimal_1_a_2, binary_to_hexadecimal_1_b_2, binary_to_hexadecimal_1_c_2,
       binary_to_hexadecimal_1_d_2, binary_to_hexadecimal_1_e, binary_to_hexadecimal_1_f,
       binary_to_hexadecimal_1_g;

  Binary_to_Hexadecimal binary_to_hexadecimal_1 (
    .A(in_1), .B(in_2), .C(in_3), .D(in_4), .a_2(binary_to_hexadecimal_1_a_2),
    .b_2(binary_to_hexadecimal_1_b_2), .c_2(binary_to_hexadecimal_1_c_2), .d_2(binary_to_hexadecimal_1_d_2),
    .e(binary_to_hexadecimal_1_e), .f(binary_to_hexadecimal_1_f), .g(binary_to_hexadecimal_1_g));
  _7_Segment_Display u_7_segment_display_1 (
    .g(binary_to_hexadecimal_1_g), .f(binary_to_hexadecimal_1_f), .a(binary_to_hexadecimal_1_a_2),
    .b(binary_to_hexadecimal_1_b_2), .e(binary_to_hexadecimal_1_e), .d(binary_to_hexadecimal_1_d_2),
    .c(binary_to_hexadecimal_1_c_2));  // open: dp
endmodule
