// Logisim project DECADE COUNTER.circ as structural Verilog: 3 circuits, main circuit main
module main (
  input  in_1,
  output _1,
  output out_3,
  output out_4,
  output out_5
);

  wire and_1_out, clock_1_out, j_k_ff_1_qn, j_k_ff_2_qn, j_k_ff_3_qn;

  Clock clock_1 (.out(clock_1_out));
  J_K_Flip_Flop j_k_ff_1 (
    .J(in_1), .clk(clock_1_out), .K(in_1), .Q(_1), .Qn(j_k_ff_1_qn), .en(in_1), .reset(and_1_out));  // open: preset
  J_K_Flip_Flop j_k_ff_2 (
    .J(in_1), .clk(j_k_ff_1_qn), .K(in_1), .Q(out_3), .Qn(j_k_ff_2_qn), .en(in_1), .reset(and_1_out));  // open: preset
  LED led_1 (.in(out_3));
  LED led_2 (.in(_1));
  J_K_Flip_Flop j_k_ff_3 (
    .J(in_1), .clk(j_k_ff_2_qn), .K(in_1), .Q(out_4), .Qn(j_k_ff_3_qn), .en(in_1), .reset(and_1_out));  // open: preset
  LED led_3 (.in(out_5));
  LED led_4 (.in(out_4));
  and and_1 (and_1_out, out_3, out_5);
  J_K_Flip_Flop j_k_ff_4 (
    .J(in_1), .clk(j_k_ff_3_qn), .K(in_1), .Q(out_5), .en(in_1), .reset(and_1_out));  // open: Qn, preset

  // Notes on the sheet:
  //   CLK
  //   2
  //   1
  //   TRUNCATED MOD10 OR DECADE COUNTER
  //   8
  //   4
endmodule

module modd10 (
  input  in_1,
  input  CLK,
  output _1,
  output out_4,
  output out_5,
  output out_6
);

  wire and_1_out, j_k_ff_1_qn, j_k_ff_2_qn, j_k_ff_3_qn;

  J_K_Flip_Flop j_k_ff_1 (
    .J(in_1), .clk(CLK), .K(in_1), .Q(_1), .Qn(j_k_ff_1_qn), .en(in_1), .reset(and_1_out));  // open: preset
  J_K_Flip_Flop j_k_ff_2 (
    .J(in_1), .clk(j_k_ff_1_qn), .K(in_1), .Q(out_4), .Qn(j_k_ff_2_qn), .en(in_1), .reset(and_1_out));  // open: preset
  LED led_1 (.in(_1));
  LED led_2 (.in(out_4));
  J_K_Flip_Flop j_k_ff_3 (
    .J(in_1), .clk(j_k_ff_2_qn), .K(in_1), .Q(out_5), .Qn(j_k_ff_3_qn), .en(in_1), .reset(and_1_out));  // open: preset
  LED led_3 (.in(out_6));
  LED led_4 (.in(out_5));
  and and_1 (and_1_out, out_4, out_6);
  J_K_Flip_Flop j_k_ff_4 (
    .J(in_1), .clk(j_k_ff_3_qn), .K(in_1), .Q(out_6), .en(in_1), .reset(and_1_out));  // open: Qn, preset

  // Notes on the sheet:
  //   2
  //   1
  //   8
  //   4
endmodule

module Implementation (
  input  in_1
);

  wire clock_1_out, main_1_a_2, main_1_b_2, main_1_c_2, main_1_d_2, main_1_e, main_1_f, main_1_g,
       modd10_1__1, modd10_1_out_4, modd10_1_out_5, modd10_1_out_6;

  modd10 modd10_1 (
    .in_1(in_1), .CLK(clock_1_out), ._1(modd10_1__1), .out_4(modd10_1_out_4), .out_5(modd10_1_out_5),
    .out_6(modd10_1_out_6));
  Clock clock_1 (.out(clock_1_out));
  BCD_to_7_Segment_Decoder_main main_1 (
    .A(modd10_1_out_6), .B(modd10_1_out_5), .C(modd10_1_out_4), .D(modd10_1__1), .a_2(main_1_a_2),
    .b_2(main_1_b_2), .c_2(main_1_c_2), .d_2(main_1_d_2), .e(main_1_e), .f(main_1_f), .g(main_1_g));
  _7_Segment_Display u_7_segment_display_1 (
    .g(main_1_g), .f(main_1_f), .a(main_1_a_2), .b(main_1_b_2), .e(main_1_e), .d(main_1_d_2), .c(main_1_c_2));  // open: dp
endmodule
